# Fritzing sketch Schematics (saved by Fritzing 0.9.2b)
circuit board: 4.16888cm x 5.06615cm
breadboards: 1

parts:
  Arduino_Micro = Arduino Micro (Rev3)
  rButton = Pushbutton [package=THT]
  pButton = Pushbutton [package=THT]
  motor = DC Motor
  buzzer = Piezo Speaker
  battery = Battery block 9V

nets (from the breadboard view):
  N1: Arduino_Micro.GND, rButton.leg1, pButton.leg1, motor.pin_2, buzzer.pin1
  N2: Arduino_Micro.D2/SDA, pButton.leg0
  N3: Arduino_Micro.D3/SCL, rButton.leg0
  N4: Arduino_Micro.D11_PWM, buzzer.pin2
  N5: Arduino_Micro.D12_PWM/A11, motor.pin_1
  N6: Arduino_Micro.MISO, battery.+
  N7: Arduino_Micro.VIN, battery.-
